# Fritzing sketch CyGarage-Model2 (saved by Fritzing 0.9.3b)
circuit board: 13.3256cm x 6.89925cm
breadboards: 2

parts:
  Huzzah_ESP8266 = Adafruit HUZZAH ESP8266 [part_number="Adafruit #2471"]
  Relay1 = Adafruit PowerRelay Feather Wing [part_number="Adafruit #3191"]
  Relay2 = Adafruit PowerRelay Feather Wing [part_number="Adafruit #3191"]
  R1 = Resistor [tolerance=±5% resistance=330 package=THT]
  R2 = Resistor [tolerance=±5% resistance=330 package=THT]
  R3 = Resistor [tolerance=±5% resistance=330 package=THT]
  R4 = Resistor [tolerance=±5% resistance=330 package=THT]
  D1 = Rectifier Diode [part_number=1N4001 package="300 mil [THT]"]
  D2 = Rectifier Diode [part_number=1N4001 package="300 mil [THT]"]
  D3 = Rectifier Diode [part_number=1N4001 package="300 mil [THT]"]
  D4 = Rectifier Diode [part_number=1N4001 package="300 mil [THT]"]
  J1 = Screw terminal - 2 pins [package=THT]
  J2 = Screw terminal - 2 pins [package=THT]
  J3 = Screw terminal - 2 pins [package=THT]
  J4 = Screw terminal - 2 pins [package=THT]
  J5 = Screw terminal - 2 pins [package=THT]
  LED2 = LED - 5mm [color="Red (633nm)" package="5 mm [THT]"]
  LED1 = LED - 5mm [color="Green (570nm)" package="5 mm [THT]"]

nets:
  N1: Huzzah_ESP8266.VIN, R1.Pin_0, R2.Pin_1, R3.Pin_0, R4.Pin_1, J5.pin1
  N2: Huzzah_ESP8266.GPIO16, R4.Pin_0, D4.anode
  N3: Huzzah_ESP8266.GPIO14, R3.Pin_1, D3.anode
  N4: Huzzah_ESP8266.GPIO12, R2.Pin_0, D2.anode
  N5: Huzzah_ESP8266.GPIO13, R1.Pin_1, D1.anode
  GND: Huzzah_ESP8266.GND, Relay1.GND, Relay2.GND, J1.pin1, J2.pin2, J3.pin1, J4.pin2, J5.pin2, LED2.cathode, LED1.cathode
  3.3V: Huzzah_ESP8266.3.3V, Relay1.3.3V, Relay2.3.3V
  N6: Huzzah_ESP8266.GPIO15, LED2.anode
  N7: Huzzah_ESP8266.GPIO2, LED1.anode
  N8: Huzzah_ESP8266.GPIO4, Relay1.A
  N9: Huzzah_ESP8266.GPIO5, Relay2.A
  N10: D1.cathode, J1.pin2
  N11: D2.cathode, J2.pin1
  N12: D3.cathode, J3.pin2
  N13: D4.cathode, J4.pin1

notes:
  WiFi Act
  Open/Ajar
  +
  -
  5VDC 1A
  CyGarage-Model2, CyGarage Main Board. Dual-door IoT garage door integration., 1.0
  Door 1 Open
  Door 1 Closed
  Door 2 Open
  Door 2 Closed
  COM
  CyGarage Model 2 Rev 1.1
  Copyright (c) 2019 Cyrus Brunner
  www.cyrusbuilt.net
  WiFi IoT Dual Garage Door Controller/Monitor
  FAB 00102 ASSY 001004
  DC1
  DC2
  DC3
  DC4

custom parts:
  Adafruit HUZZAH ESP8266: Add Internet to your next project with an adorable, bite-sized WiFi microcontroller, at a price you like! The ESP8266 processor from Espressif is an 80 MHz microcontroller with a full WiFi front-end (both as client and access point) and TCP/IP stack with DNS support as well. While this chip has been very popular, its also been very difficult to use. Most of the low cost modules are not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
  Adafruit PowerRelay Feather Wing: A Feather board without ambition is a Feather board without FeatherWings! This is the Power Relay FeatherWing. It gives you power to control, and control over power. Put simply, you can now turn on and off lamps, fans, solenoids, and other small appliances that run on up to 250VAC or DC power using any Feather board. Compared to our smaller Relay FeatherWings, this one can handle a beefy 1200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
